// Logisim project project.circ as structural Verilog: 2 circuits, main circuit main
module main (
);

  wire button_1_out, clock_1_out;

  Clock clock_1 (.out(clock_1_out));
  Register register_1 (.clk(clock_1_out), .clr(button_1_out));  // open: D, en, Q
  Button button_1 (.out(button_1_out));
  ROM rom_1 ();  // open: addr, data, sel
  registradores registradores_1 ();  // open: clk, rw, reset, RW_2
  RAM ram_1 ();  // open: addr, data, sel, clk, ld, clr
endmodule

module registradores (
  input  reset,
  input  clk,
  input  rw,
  input  [3:0] RW_2
);
endmodule
